// Digital circuit D-flip-flop.dig as structural Verilog
// when clock is 1, flip-flop stores the value of D
module D_flip_flop (
  input  D,
  input  CLK,
  output Q,
  output Q_2
);

  wire and_1_out, and_2_out, not_1_out;

  not not_1 (not_1_out, D);
  and and_1 (and_1_out, not_1_out, CLK);
  and and_2 (and_2_out, CLK, D);
  nor_flip_flop nor_flip_flop_1 (.S(and_2_out), .R(and_1_out), .Q(Q), .Q_2(Q_2));

  // Notes on the sheet:
  //   D: data to save
endmodule

/* Test case:
CLK D Q -Q
  0 0 x x
  0 1 x x
  1 1 1 0
  0 1 1 0
  1 1 1 0
  1 0 0 1
  0 0 0 1
  0 1 0 1
*/
