// Digital circuit alu.dig as structural Verilog
module alu (
  input  a_0,
  input  a_1,
  input  a_2,
  input  a_3,
  input  su,
  input  b_0,
  input  b_1,
  input  b_2,
  input  b_3,
  output O_0,
  output O_1,
  output O_2,
  output O_3,
  output c_out
);

  wire adder_1_p14, xor_1_out, xor_2_out, xor_3_out, xor_4_out;

  xor xor_1 (xor_1_out, b_0, su);
  xor xor_2 (xor_2_out, b_1, su);
  xor xor_3 (xor_3_out, b_2, su);
  xor xor_4 (xor_4_out, b_3, su);
  // adder adder_1: pin names not known; wires that end beside it: su, a_0, a_1, a_2, a_3, xor_1_out, xor_2_out, xor_3_out, xor_4_out, O_0, O_1, O_2, O_3, adder_1_p14
  xor xor_5 (c_out, adder_1_p14, su);

  // Notes on the sheet:
  //   su: subtract when 1; add when 0
endmodule

/* Test case:
su a_3 a_2 a_1 a_0 b_3 b_2 b_1 b_0 c_out O_3 O_2 O_1 O_0
loop(a, 16)
  loop(b, 16)
     0 bits(4,a) bits(4,b) bits(5, a+b)
     1 bits(4,a) bits(4,b) bits(5, a-b)
  end loop
end loop
*/
