// Digital circuit counter.dig as structural Verilog
module counter (
  input  C,
  output O_0,
  output O_1,
  output O_2,
  output O_3
);

  wire t_flip_flop_1_q_2, t_flip_flop_2_q_2, t_flip_flop_3_q_2, t_flip_flop_4_q_2;

  t_flip_flop t_flip_flop_1 (.C(C), .Q_2(t_flip_flop_1_q_2));  // open: Q
  not not_1 (O_0, t_flip_flop_1_q_2);
  t_flip_flop t_flip_flop_2 (.C(t_flip_flop_1_q_2), .Q_2(t_flip_flop_2_q_2));  // open: Q
  not not_2 (O_1, t_flip_flop_2_q_2);
  t_flip_flop t_flip_flop_3 (.C(t_flip_flop_2_q_2), .Q_2(t_flip_flop_3_q_2));  // open: Q
  not not_3 (O_2, t_flip_flop_3_q_2);
  t_flip_flop t_flip_flop_4 (.C(t_flip_flop_3_q_2), .Q_2(t_flip_flop_4_q_2));  // open: Q
  not not_4 (O_3, t_flip_flop_4_q_2);

  // Notes on the sheet:
  //   IC: tick, set to value, set to zero
  //   MIC: tick, set to zero
  //   reg: set value
  //   options:
  //   1. use simplest counter (no set / reset);
  //   .   easy for testing bus and see first effects of reading mem
  //   .   then repladce with whatever needed
  //   2. add full-featured IC counter, use forboth counters, later simplify
  //   3. make simple smaller MIC to test basic functionality, then add set for jump
endmodule
