// Digital circuit cpu.dig as structural Verilog
module cpu (
  input  in_1,
  input  in_2,
  input  in_3,
  input  clk
);

  wire adder_1_p10, adder_1_p11, adder_2_p11, adder_2_p12, adder_2_p13, adder_2_p14, alu_out, and_1_out,
       and_2_out, and_3_out, and_4_out, and_5_out, and_6_out, button_1_out, button_2_out, carry,
       counter_resetable_1_o_0, counter_resetable_1_o_1, counter_resetable_1_o_2, counter_resetable_1_o_3,
       counter_resetable_2_o_0, counter_resetable_2_o_1, counter_resetable_2_o_2, counter_resetable_2_o_3,
       Current_Instruction_HI_q_0, Current_Instruction_HI_q_1, Current_Instruction_HI_q_2,
       Current_Instruction_HI_q_3, Current_Instruction_LO_q_0, Current_Instruction_LO_q_1,
       Current_Instruction_LO_q_2, Current_Instruction_LO_q_3, decoder_6_to_64_1_o_0, decoder_6_to_64_1_o_1,
       decoder_6_to_64_1_o_2, decoder_6_to_64_1_o_3, decoder_6_to_64_1_o_4, decoder_6_to_64_1_o_5,
       decoder_6_to_64_1_o_6, decoder_6_to_64_1_o_7, decoder_6_to_64_1_o_8, decoder_6_to_64_1_o_9,
       decoder_6_to_64_1_o_10, decoder_6_to_64_1_o_11, decoder_6_to_64_1_o_12, decoder_6_to_64_1_o_13,
       decoder_6_to_64_1_o_14, decoder_6_to_64_1_o_15, decoder_6_to_64_1_o_16, decoder_6_to_64_1_o_17,
       decoder_6_to_64_1_o_18, decoder_6_to_64_1_o_19, decoder_6_to_64_1_o_24, decoder_6_to_64_1_o_25,
       decoder_6_to_64_1_o_26, decoder_6_to_64_1_o_27, decoder_6_to_64_1_o_32, decoder_6_to_64_1_o_33,
       decoder_6_to_64_1_o_34, decoder_6_to_64_1_o_35, decoder_6_to_64_1_o_36, decoder_6_to_64_1_o_37,
       decoder_6_to_64_1_o_38, decoder_6_to_64_1_o_39, decoder_6_to_64_1_o_40, decoder_6_to_64_1_o_41,
       decoder_6_to_64_1_o_42, decoder_6_to_64_1_o_43, decoder_6_to_64_1_o_48, decoder_6_to_64_1_o_49,
       decoder_6_to_64_1_o_50, decoder_6_to_64_1_o_51, decoder_6_to_64_1_o_56, decoder_6_to_64_1_o_57,
       decoder_6_to_64_1_o_58, decoder_6_to_64_1_o_59, delay_1_out, madr_q_0, madr_q_1, madr_q_2, madr_q_3,
       memory2_1_o_0, memory2_1_o_1, memory2_1_o_2, memory2_1_o_3, memory2_1_o_4, memory2_1_o_5,
       memory2_1_o_6, memory2_1_o_7, nor_1_out, nor_2_out, not_1_out, not_2_out, not_3_out, not_4_out,
       not_5_out, not_6_out, not_7_out, or_1_out, pc_reset, register_simple_1_q_0, register_simple_1_q_1,
       register_simple_1_q_2, register_simple_1_q_3, register_simple_2_q_0, register_simple_2_q_1,
       register_simple_2_q_2, register_simple_2_q_3, tri_state_buffer_4bit_1_o_0,
       tri_state_buffer_4bit_1_o_1, tri_state_buffer_4bit_1_o_2, tri_state_buffer_4bit_1_o_3,
       tri_state_buffer_4bit_2_o_0, tri_state_buffer_4bit_2_o_1, tri_state_buffer_4bit_2_o_2,
       tri_state_buffer_4bit_2_o_3;
  wire [15:0] control_bus;

  Delay #(.delayTime(20), .generic("this.Duration = args.duration;")) delay_1 (.in(button_1_out), .out(delay_1_out));
  Button #(.activeLow("true")) button_1 (.out(button_1_out));
  Button button_2 (.out(button_2_out));
  not not_1 (not_1_out, delay_1_out);
  or or_1 (or_1_out, control_bus[4], clk);
  and and_1 (and_1_out, button_1_out, not_1_out);
  or or_2 (pc_reset, and_1_out, in_3, button_2_out);
  not not_2 (not_2_out, pc_reset);
  not not_3 (not_3_out, or_1_out);
  and and_2 (and_2_out, not_2_out, not_3_out);
  counter_resetable counter_resetable_1 (
    .C(or_1_out), .R(and_5_out), .S(1'b0), .D_0(1'b0), .D_1(1'b0), .D_2(1'b0), .D_3(1'b0), .R_a(pc_reset),
    .O_0(counter_resetable_1_o_0), .O_1(counter_resetable_1_o_1), .O_2(counter_resetable_1_o_2),
    .O_3(counter_resetable_1_o_3));
  not not_4 (not_4_out, counter_resetable_1_o_0);
  not not_5 (not_5_out, counter_resetable_1_o_1);
  not not_6 (not_6_out, counter_resetable_1_o_2);
  not not_7 (not_7_out, counter_resetable_1_o_3);
  and and_3 (and_3_out, not_4_out, not_5_out, not_6_out, not_7_out);
  and and_4 (and_4_out, counter_resetable_1_o_0, not_5_out, not_6_out, not_7_out);
  and and_5 (and_5_out, counter_resetable_1_o_0, counter_resetable_1_o_2);
  // adder adder_1: pin names not known; wires that end beside it: 1'b0, 1'b0, 1'b1, 1'b0, 1'b0, counter_resetable_1_o_0, counter_resetable_1_o_1, counter_resetable_1_o_2, counter_resetable_1_o_3, adder_1_p10, adder_1_p11
  assign control_bus[0] = and_3_out ? and_3_out : 1'bz;  // Driver driver_1
  assign control_bus[1] = and_3_out ? and_3_out : 1'bz;  // Driver driver_2
  assign control_bus[3] = and_4_out ? and_4_out : 1'bz;  // Driver driver_3
  assign control_bus[6] = and_4_out ? and_4_out : 1'bz;  // Driver driver_4
  assign control_bus[2] = and_4_out ? and_4_out : 1'bz;  // Driver driver_5
  PullDown pulldown_1 (.out(control_bus[10]));
  PullDown pulldown_2 (.out(control_bus[11]));
  PullDown pulldown_3 (.out(control_bus[6]));
  PullDown pulldown_4 (.out(alu_out));
  PullDown pulldown_5 (.out(control_bus[8]));
  PullDown pulldown_6 (.out(control_bus[9]));
  PullDown pulldown_7 (.out(control_bus[2]));
  PullDown pulldown_8 (.out(control_bus[3]));
  PullDown pulldown_9 (.out(control_bus[4]));
  PullDown pulldown_10 (.out(control_bus[5]));
  nor nor_1 (nor_1_out, and_3_out, and_4_out);
  PullDown pulldown_11 (.out(control_bus[0]));
  PullDown pulldown_12 (.out(control_bus[1]));
  Break break_1 (.brk(nor_1_out));
  decoder_6_to_64 decoder_6_to_64_1 (
    .S_0(adder_1_p10), .S_1(adder_1_p11), .S_2(Current_Instruction_HI_q_0), .S_3(Current_Instruction_HI_q_1),
    .S_4(Current_Instruction_HI_q_2), .S_5(Current_Instruction_HI_q_3), .E(nor_1_out),
    .O_0(decoder_6_to_64_1_o_0), .O_1(decoder_6_to_64_1_o_1), .O_2(decoder_6_to_64_1_o_2),
    .O_3(decoder_6_to_64_1_o_3), .O_4(decoder_6_to_64_1_o_4), .O_5(decoder_6_to_64_1_o_5),
    .O_6(decoder_6_to_64_1_o_6), .O_7(decoder_6_to_64_1_o_7), .O_8(decoder_6_to_64_1_o_8),
    .O_9(decoder_6_to_64_1_o_9), .O_10(decoder_6_to_64_1_o_10), .O_11(decoder_6_to_64_1_o_11),
    .O_12(decoder_6_to_64_1_o_12), .O_13(decoder_6_to_64_1_o_13), .O_14(decoder_6_to_64_1_o_14),
    .O_15(decoder_6_to_64_1_o_15), .O_16(decoder_6_to_64_1_o_16), .O_17(decoder_6_to_64_1_o_17),
    .O_18(decoder_6_to_64_1_o_18), .O_19(decoder_6_to_64_1_o_19), .O_24(decoder_6_to_64_1_o_24),
    .O_25(decoder_6_to_64_1_o_25), .O_26(decoder_6_to_64_1_o_26), .O_27(decoder_6_to_64_1_o_27),
    .O_32(decoder_6_to_64_1_o_32), .O_33(decoder_6_to_64_1_o_33), .O_34(decoder_6_to_64_1_o_34),
    .O_35(decoder_6_to_64_1_o_35), .O_36(decoder_6_to_64_1_o_36), .O_37(decoder_6_to_64_1_o_37),
    .O_38(decoder_6_to_64_1_o_38), .O_39(decoder_6_to_64_1_o_39), .O_40(decoder_6_to_64_1_o_40),
    .O_41(decoder_6_to_64_1_o_41), .O_42(decoder_6_to_64_1_o_42), .O_43(decoder_6_to_64_1_o_43),
    .O_48(decoder_6_to_64_1_o_48), .O_49(decoder_6_to_64_1_o_49), .O_50(decoder_6_to_64_1_o_50),
    .O_51(decoder_6_to_64_1_o_51), .O_56(decoder_6_to_64_1_o_56), .O_57(decoder_6_to_64_1_o_57),
    .O_58(decoder_6_to_64_1_o_58), .O_59(decoder_6_to_64_1_o_59));  // open: O_20, O_21, O_22, O_23, O_28, O_29, O_30, O_31, O_44, O_45, O_46, O_47, O_52, O_53, O_54, O_55, O_60, O_61, O_62, O_63
  assign {control_bus[15:8], alu_out, control_bus[6:0]} = decoder_6_to_64_1_o_9 ? 16'h24 : 16'bz;  // Driver driver_6
  assign {control_bus[15:8], alu_out, control_bus[6:0]} = decoder_6_to_64_1_o_13 ? 16'h204 : 16'bz;  // Driver driver_7
  assign {control_bus[15:8], alu_out, control_bus[6:0]} = decoder_6_to_64_1_o_17 ? 16'h480 : 16'bz;  // Driver driver_8
  assign {control_bus[15:8], alu_out, control_bus[6:0]} = decoder_6_to_64_1_o_25 ? 16'hc00 : 16'bz;  // Driver driver_9
  assign {control_bus[15:8], alu_out, control_bus[6:0]} = decoder_6_to_64_1_o_37 ? 16'ha0 : 16'bz;  // Driver driver_10
  assign {control_bus[15:8], alu_out, control_bus[6:0]} = decoder_6_to_64_1_o_42 ? 16'ha0 : 16'bz;  // Driver driver_11
  assign {control_bus[15:8], alu_out, control_bus[6:0]} = decoder_6_to_64_1_o_0 ? 16'h10 : 16'bz;  // Driver driver_12
  assign {control_bus[15:8], alu_out, control_bus[6:0]} = decoder_6_to_64_1_o_4 ? 16'h24 : 16'bz;  // Driver driver_13
  assign {control_bus[15:8], alu_out, control_bus[6:0]} = decoder_6_to_64_1_o_8 ? 16'h6 : 16'bz;  // Driver driver_14
  assign {control_bus[15:8], alu_out, control_bus[6:0]} = decoder_6_to_64_1_o_12 ? 16'h6 : 16'bz;  // Driver driver_15
  assign {control_bus[15:8], alu_out, control_bus[6:0]} = decoder_6_to_64_1_o_16 ? 16'h6 : 16'bz;  // Driver driver_16
  assign {control_bus[15:8], alu_out, control_bus[6:0]} = decoder_6_to_64_1_o_24 ? 16'h6 : 16'bz;  // Driver driver_17
  assign {control_bus[15:8], alu_out, control_bus[6:0]} = decoder_6_to_64_1_o_32 ? 16'h810 : 16'bz;  // Driver driver_18
  assign {control_bus[15:8], alu_out, control_bus[6:0]} = decoder_6_to_64_1_o_36 ? 16'h204 : 16'bz;  // Driver driver_19
  assign {control_bus[15:8], alu_out, control_bus[6:0]} = decoder_6_to_64_1_o_40 ? 16'h6 : 16'bz;  // Driver driver_20
  assign {control_bus[15:8], alu_out, control_bus[6:0]} = decoder_6_to_64_1_o_41 ? 16'h204 : 16'bz;  // Driver driver_21
  assign {control_bus[15:8], alu_out, control_bus[6:0]} = decoder_6_to_64_1_o_48 ? 16'h144 : 16'bz;  // Driver driver_22
  assign {control_bus[15:8], alu_out, control_bus[6:0]} = decoder_6_to_64_1_o_56 ? {{7{1'b0}}, carry, 1'b0, carry, 6'b000100} : 16'bz;  // Driver driver_23
  register_simple madr (
    .E_out(control_bus[1]), .CLK(and_2_out), .D_0(tri_state_buffer_4bit_1_o_0),
    .D_1(tri_state_buffer_4bit_1_o_1), .D_2(tri_state_buffer_4bit_1_o_2), .D_3(tri_state_buffer_4bit_1_o_3),
    .Q_0(madr_q_0), .Q_1(madr_q_1), .Q_2(madr_q_2), .Q_3(madr_q_3));
  memory2 memory2_1 (
    .a_0(madr_q_0), .a_1(madr_q_1), .a_2(madr_q_2), .a_3(madr_q_3), .E(control_bus[10]), .C(and_2_out),
    .D_0(tri_state_buffer_4bit_1_o_0), .D_1(tri_state_buffer_4bit_1_o_1), .D_2(tri_state_buffer_4bit_1_o_2),
    .D_3(tri_state_buffer_4bit_1_o_3), .O_0(memory2_1_o_0), .O_1(memory2_1_o_1), .O_2(memory2_1_o_2),
    .O_3(memory2_1_o_3), .O_4(memory2_1_o_4), .O_5(memory2_1_o_5), .O_6(memory2_1_o_6), .O_7(memory2_1_o_7));
  tri_state_buffer_4bit tri_state_buffer_4bit_1 (
    .D_0(memory2_1_o_0), .D_1(memory2_1_o_1), .D_2(memory2_1_o_2), .D_3(memory2_1_o_3), .E(control_bus[2]),
    .O_0(tri_state_buffer_4bit_1_o_0), .O_1(tri_state_buffer_4bit_1_o_1), .O_2(tri_state_buffer_4bit_1_o_2),
    .O_3(tri_state_buffer_4bit_1_o_3));
  tri_state_buffer_4bit tri_state_buffer_4bit_2 (
    .D_0(memory2_1_o_4), .D_1(memory2_1_o_5), .D_2(memory2_1_o_6), .D_3(memory2_1_o_7), .E(control_bus[2]),
    .O_0(tri_state_buffer_4bit_2_o_0), .O_1(tri_state_buffer_4bit_2_o_1), .O_2(tri_state_buffer_4bit_2_o_2),
    .O_3(tri_state_buffer_4bit_2_o_3));
  register_simple Current_Instruction_HI (
    .E_out(control_bus[3]), .CLK(and_2_out), .D_0(tri_state_buffer_4bit_2_o_0),
    .D_1(tri_state_buffer_4bit_2_o_1), .D_2(tri_state_buffer_4bit_2_o_2), .D_3(tri_state_buffer_4bit_2_o_3),
    .Q_0(Current_Instruction_HI_q_0), .Q_1(Current_Instruction_HI_q_1), .Q_2(Current_Instruction_HI_q_2),
    .Q_3(Current_Instruction_HI_q_3));
  register_simple Current_Instruction_LO (
    .E_out(control_bus[3]), .CLK(and_2_out), .D_0(tri_state_buffer_4bit_1_o_0),
    .D_1(tri_state_buffer_4bit_1_o_1), .D_2(tri_state_buffer_4bit_1_o_2), .D_3(tri_state_buffer_4bit_1_o_3),
    .Q_0(Current_Instruction_LO_q_0), .Q_1(Current_Instruction_LO_q_1), .Q_2(Current_Instruction_LO_q_2),
    .Q_3(Current_Instruction_LO_q_3));
  and and_6 (and_6_out, control_bus[6], and_2_out);
  counter_resetable counter_resetable_2 (
    .C(and_6_out), .R(1'b0), .S(control_bus[8]), .D_0(tri_state_buffer_4bit_1_o_0),
    .D_1(tri_state_buffer_4bit_1_o_1), .D_2(tri_state_buffer_4bit_1_o_2), .D_3(tri_state_buffer_4bit_1_o_3),
    .R_a(pc_reset), .O_0(counter_resetable_2_o_0), .O_1(counter_resetable_2_o_1),
    .O_2(counter_resetable_2_o_2), .O_3(counter_resetable_2_o_3));
  tri_state_buffer_4bit tri_state_buffer_4bit_3 (
    .D_0(counter_resetable_2_o_0), .D_1(counter_resetable_2_o_1), .D_2(counter_resetable_2_o_2),
    .D_3(counter_resetable_2_o_3), .E(control_bus[0]), .O_0(tri_state_buffer_4bit_1_o_0),
    .O_1(tri_state_buffer_4bit_1_o_1), .O_2(tri_state_buffer_4bit_1_o_2), .O_3(tri_state_buffer_4bit_1_o_3));
  register_simple register_simple_1 (
    .E_out(control_bus[5]), .CLK(and_2_out), .D_0(tri_state_buffer_4bit_1_o_0),
    .D_1(tri_state_buffer_4bit_1_o_1), .D_2(tri_state_buffer_4bit_1_o_2), .D_3(tri_state_buffer_4bit_1_o_3),
    .Q_0(register_simple_1_q_0), .Q_1(register_simple_1_q_1), .Q_2(register_simple_1_q_2),
    .Q_3(register_simple_1_q_3));
  register_simple register_simple_2 (
    .E_out(control_bus[9]), .CLK(and_2_out), .D_0(tri_state_buffer_4bit_1_o_0),
    .D_1(tri_state_buffer_4bit_1_o_1), .D_2(tri_state_buffer_4bit_1_o_2), .D_3(tri_state_buffer_4bit_1_o_3),
    .Q_0(register_simple_2_q_0), .Q_1(register_simple_2_q_1), .Q_2(register_simple_2_q_2),
    .Q_3(register_simple_2_q_3));
  tri_state_buffer_4bit tri_state_buffer_4bit_4 (
    .D_0(adder_2_p11), .D_1(adder_2_p12), .D_2(adder_2_p13), .D_3(adder_2_p14), .E(alu_out),
    .O_0(tri_state_buffer_4bit_1_o_0), .O_1(tri_state_buffer_4bit_1_o_1), .O_2(tri_state_buffer_4bit_1_o_2),
    .O_3(tri_state_buffer_4bit_1_o_3));
  tri_state_buffer_4bit tri_state_buffer_4bit_5 (
    .D_0(register_simple_1_q_0), .D_1(register_simple_1_q_1), .D_2(register_simple_1_q_2),
    .D_3(register_simple_1_q_3), .E(control_bus[11]), .O_0(tri_state_buffer_4bit_1_o_0),
    .O_1(tri_state_buffer_4bit_1_o_1), .O_2(tri_state_buffer_4bit_1_o_2), .O_3(tri_state_buffer_4bit_1_o_3));
  tri_state_buffer_4bit tri_state_buffer_4bit_6 (
    .D_0(register_simple_2_q_0), .D_1(register_simple_2_q_1), .D_2(register_simple_2_q_2),
    .D_3(register_simple_2_q_3), .E(in_1), .O_0(tri_state_buffer_4bit_1_o_0),
    .O_1(tri_state_buffer_4bit_1_o_1), .O_2(tri_state_buffer_4bit_1_o_2), .O_3(tri_state_buffer_4bit_1_o_3));
  nor nor_2 (nor_2_out, register_simple_1_q_3, register_simple_1_q_2, register_simple_1_q_1, register_simple_1_q_0);
  // adder adder_2: pin names not known; wires that end beside it: nor_2_out, in_2, register_simple_1_q_0, register_simple_1_q_1, register_simple_1_q_2, register_simple_1_q_3, register_simple_2_q_0, register_simple_2_q_1, register_simple_2_q_2, register_simple_2_q_3, adder_2_p11, adder_2_p12, adder_2_p13, adder_2_p14, carry

  // Other names for the same wires on the sheet: pc_out = control_bus[0]; madr_in = control_bus[1];
  //   mem_out = control_bus[2]; curr_instr_in = control_bus[3]; halt = control_bus[4]; reg_A_in = control_bus[5];
  //   pc_inc = control_bus[6]; control_bus[7] = alu_out; pc_in = control_bus[8]; reg_B_in = control_bus[9];
  //   mem_in = control_bus[10]; reg_A_out = control_bus[11]

  // Notes on the sheet:
  //   clk: Hz: 100
  //   1110 jc imm: jump if carry==1 to imm
  //   mem-out; (pc-in and carry) , (pc-inc and (clock))
  //   1100 jmp imm: 
  //   pc-in; mem-out, pc-inc (clock)
  //   0001 load imm to A
  //   .   mem-out, A-in
  //   0010 load mem[imm] to A
  //   .   mem-out, madr-in
  //   .   mem-out, regA-in
  //   0011 load mem[imm] to B
  //   .   mem-out, madr-in
  //   .   mem-out, regB-in
  //   0100 store regA+regB to mem[imm]
  //   .   mem-out, madr-in
  //   .   alu-out, mem-in
  //   0110 store regA to mem[imm]
  //       mem-out, madr-in
  //   .   reg-A-out, mem-in
  //   increase A by imm (1001)
  //   alu-out, mem-in,
  //   alu-out, regA-in
  //   increase A by mem[imm] (1010)
  //   mem-out, madr-in
  //   mem-out, reg-B-in,
  //   alu-out, regA-in
  //   0000 halt
  //   1000 halt-out regA
  //   .  reg-A-out, hlt
endmodule
