// Digital circuit decoder-2-to-4.dig as structural Verilog
module decoder_2_to_4 (
  input  S_0,
  input  S_1,
  input  E,
  output O_0,
  output O_1,
  output O_2,
  output O_3
);

  wire not_1_out, not_2_out;

  not not_1 (not_1_out, S_0);
  not not_2 (not_2_out, S_1);
  and and_1 (O_0, E, not_1_out, not_2_out);
  and and_2 (O_1, E, S_0, not_2_out);
  and and_3 (O_2, E, S_1, not_1_out);
  and and_4 (O_3, E, S_1, S_0);
endmodule

/* Test case:
E S_1 S_0  O_0 O_1 O_2 O_3

0 x   x       0 0 0 0
1  0 0  1 0 0 0
1  0 1  0 1 0 0
1  1 0  0 0 1 0
1  1 1  0 0 0 1
*/
