// Digital circuit decoder-6-to-64.dig as structural Verilog
module decoder_6_to_64 (
  input  S_0,
  input  S_1,
  input  S_2,
  input  S_3,
  input  S_4,
  input  S_5,
  input  E,
  output O_0,
  output O_1,
  output O_2,
  output O_3,
  output O_4,
  output O_5,
  output O_6,
  output O_7,
  output O_8,
  output O_9,
  output O_10,
  output O_11,
  output O_12,
  output O_13,
  output O_14,
  output O_15,
  output O_16,
  output O_17,
  output O_18,
  output O_19,
  output O_20,
  output O_21,
  output O_22,
  output O_23,
  output O_24,
  output O_25,
  output O_26,
  output O_27,
  output O_28,
  output O_29,
  output O_30,
  output O_31,
  output O_32,
  output O_33,
  output O_34,
  output O_35,
  output O_36,
  output O_37,
  output O_38,
  output O_39,
  output O_40,
  output O_41,
  output O_42,
  output O_43,
  output O_44,
  output O_45,
  output O_46,
  output O_47,
  output O_48,
  output O_49,
  output O_50,
  output O_51,
  output O_52,
  output O_53,
  output O_54,
  output O_55,
  output O_56,
  output O_57,
  output O_58,
  output O_59,
  output O_60,
  output O_61,
  output O_62,
  output O_63
);

  wire and_1_out, and_2_out, and_3_out, and_4_out, and_5_out, and_6_out, and_7_out, and_8_out, not_1_out,
       not_2_out, not_3_out;

  not not_1 (not_1_out, S_3);
  not not_2 (not_2_out, S_4);
  not not_3 (not_3_out, S_5);
  and and_1 (and_1_out, E, not_1_out, not_2_out, not_3_out);
  and and_2 (and_2_out, E, S_3, not_2_out, not_3_out);
  and and_3 (and_3_out, E, not_1_out, S_4, not_3_out);
  and and_4 (and_4_out, E, S_3, S_4, not_3_out);
  and and_5 (and_5_out, E, not_1_out, not_2_out, S_5);
  and and_6 (and_6_out, E, S_3, not_2_out, S_5);
  and and_7 (and_7_out, E, not_1_out, S_4, S_5);
  and and_8 (and_8_out, E, S_3, S_4, S_5);
  decoder_3_to_8 decoder_3_to_8_1 (
    .S_0(S_0), .S_1(S_1), .S_2(S_2), .E(and_1_out), .O_0(O_0), .O_1(O_1), .O_2(O_2), .O_3(O_3), .O_4(O_4),
    .O_5(O_5), .O_6(O_6), .O_7(O_7));
  decoder_3_to_8 decoder_3_to_8_2 (
    .S_0(S_0), .S_1(S_1), .S_2(S_2), .E(and_2_out), .O_0(O_8), .O_1(O_9), .O_2(O_10), .O_3(O_11), .O_4(O_12),
    .O_5(O_13), .O_6(O_14), .O_7(O_15));
  decoder_3_to_8 decoder_3_to_8_3 (
    .S_0(S_0), .S_1(S_1), .S_2(S_2), .E(and_3_out), .O_0(O_16), .O_1(O_17), .O_2(O_18), .O_3(O_19),
    .O_4(O_20), .O_5(O_21), .O_6(O_22), .O_7(O_23));
  decoder_3_to_8 decoder_3_to_8_4 (
    .S_0(S_0), .S_1(S_1), .S_2(S_2), .E(and_4_out), .O_0(O_24), .O_1(O_25), .O_2(O_26), .O_3(O_27),
    .O_4(O_28), .O_5(O_29), .O_6(O_30), .O_7(O_31));
  decoder_3_to_8 decoder_3_to_8_5 (
    .S_0(S_0), .S_1(S_1), .S_2(S_2), .E(and_5_out), .O_0(O_32), .O_1(O_33), .O_2(O_34), .O_3(O_35),
    .O_4(O_36), .O_5(O_37), .O_6(O_38), .O_7(O_39));
  decoder_3_to_8 decoder_3_to_8_6 (
    .S_0(S_0), .S_1(S_1), .S_2(S_2), .E(and_6_out), .O_0(O_40), .O_1(O_41), .O_2(O_42), .O_3(O_43),
    .O_4(O_44), .O_5(O_45), .O_6(O_46), .O_7(O_47));
  decoder_3_to_8 decoder_3_to_8_7 (
    .S_0(S_0), .S_1(S_1), .S_2(S_2), .E(and_7_out), .O_0(O_48), .O_1(O_49), .O_2(O_50), .O_3(O_51),
    .O_4(O_52), .O_5(O_53), .O_6(O_54), .O_7(O_55));
  decoder_3_to_8 decoder_3_to_8_8 (
    .S_0(S_0), .S_1(S_1), .S_2(S_2), .E(and_8_out), .O_0(O_56), .O_1(O_57), .O_2(O_58), .O_3(O_59),
    .O_4(O_60), .O_5(O_61), .O_6(O_62), .O_7(O_63));
endmodule

/* Test case:
E  S_5 S_4 S_3 S_2 S_1 S_0  O_63 O_62 O_61 O_60 O_59 O_58 O_57 O_56 O_55 O_54 O_53 O_52 O_51 O_50 O_49 O_48 O_47 O_46 O_45 O_44 O_43 O_42 O_41 O_40 O_39 O_38 O_37 O_36 O_35 O_34 O_33 O_32 O_31 O_30 O_29 O_28 O_27 O_26 O_25 O_24 O_23 O_22 O_21 O_20 O_19 O_18 O_17 O_16 O_15 O_14 O_13 O_12 O_11 O_10 O_9 O_8 O_7 O_6 O_5 O_4 O_3 O_2 O_1 O_0
0   x x x x x x   bits(64, 0)
repeat(64) 1 bits(6, n) bits(64, 1<<n)
*/
