// Digital circuit JK-async-resetable-flip-flop.dig as structural Verilog
module JK_async_resetable_flip_flop (
  input  C,
  input  S,
  input  R,
  input  R_a,
  output Q,
  output Q_2
);

  wire and_1_out, and_2_out, and_3_out, and_4_out, nor_1_out, nor_2_out, not_1_out, not_2_out, or_1_out,
       or_2_out;

  and and_1 (and_1_out, S, Q_2, C);
  and and_2 (and_2_out, C, Q, R);
  or or_1 (or_1_out, 1'b0, and_1_out);
  or or_2 (or_2_out, and_2_out, R_a);
  nor nor_1 (nor_1_out, or_1_out, nor_2_out);
  nor nor_2 (nor_2_out, nor_1_out, or_2_out);
  not not_1 (not_1_out, C);
  not not_2 (not_2_out, R_a);
  and and_3 (and_3_out, nor_2_out, not_2_out, not_1_out);
  and and_4 (and_4_out, not_1_out, nor_1_out);
  nor nor_3 (Q_2, and_3_out, 1'b0, Q);
  nor nor_4 (Q, Q_2, R_a, and_4_out);

  // Notes on the sheet:
  //   S: set
  //   R: reset
  //   R_a: async reset
  //   rising edge toggling JK flip-flop without delay
endmodule
