// Digital circuit adder.dig as structural Verilog
module adder (
  input  c_in,
  input  a_0,
  input  a_1,
  input  a_2,
  input  a_3,
  input  b_0,
  input  b_1,
  input  b_2,
  input  b_3,
  output o_0,
  output o_1,
  output o_2,
  output o_3,
  output c_out
);

  wire full_adder_1_c_out, full_adder_2_c_out, full_adder_3_c_out;

  full_adder full_adder_1 (.c_in(c_in), .i_1(a_0), .i_2(b_0), .o(o_0), .c_out(full_adder_1_c_out));
  full_adder full_adder_2 (.c_in(full_adder_1_c_out), .i_1(a_1), .i_2(b_1), .o(o_1), .c_out(full_adder_2_c_out));
  full_adder full_adder_3 (.c_in(full_adder_2_c_out), .i_1(a_2), .i_2(b_2), .o(o_2), .c_out(full_adder_3_c_out));
  full_adder full_adder_4 (.c_in(full_adder_3_c_out), .i_1(a_3), .i_2(b_3), .o(o_3), .c_out(c_out));

  // Notes on the sheet:
  //   c_in: 1 when we add 1 from previous operation
endmodule

/* Test case 4bit adder test:
        c_in a_3 a_2 a_1 a_0 b_3 b_2 b_1 b_0    c_out o_3 o_2 o_1 o_0

loop(c, 2)
 loop(a, 16)
  loop(b, 16)
        (c) bits(4, a) bits(4, b) bits(5, a+b+c)
  end loop
 end loop
end loop
*/
