// Digital circuit buffered-8bit-register.dig as structural Verilog
// memory location that can be selected for read (tri-state enabled)
//  or (selected for read (tri-state enabled) and enabled for write)
module buffered_8bit_register (
  input  CLK,
  input  E_store,
  input  E_ouput,
  input  D_0,
  input  D_1,
  input  D_2,
  input  D_3,
  output O_0,
  output O_1,
  output O_2,
  output O_3,
  output O_4,
  output O_5,
  output O_6,
  output O_7
);

  wire and_1_out, register_simple_1_q_0, register_simple_1_q_1, register_simple_1_q_2, register_simple_1_q_3;

  and and_1 (and_1_out, E_store, E_ouput);
  register_simple register_simple_1 (
    .E_out(and_1_out), .CLK(CLK), .D_0(D_0), .D_1(D_1), .D_2(D_2), .D_3(D_3), .Q_0(register_simple_1_q_0),
    .Q_1(register_simple_1_q_1), .Q_2(register_simple_1_q_2), .Q_3(register_simple_1_q_3));
  tri_state_buffer_4bit tri_state_buffer_4bit_1 (
    .D_0(register_simple_1_q_0), .D_1(register_simple_1_q_1), .D_2(register_simple_1_q_2),
    .D_3(register_simple_1_q_3), .E(E_ouput), .O_0(O_0), .O_1(O_1), .O_2(O_2), .O_3(O_3));
  tri_state_buffer_4bit tri_state_buffer_4bit_2 (
    .D_0(1'b0), .D_1(1'b0), .D_2(1'b0), .D_3(1'b0), .E(E_ouput), .O_0(O_4), .O_1(O_5), .O_2(O_6), .O_3(O_7));
endmodule
