// Digital circuit buffered-register.dig as structural Verilog
module buffered_register (
  input  E_ouput,
  input  E_store,
  input  CLK,
  input  D_0,
  input  D_1,
  input  D_2,
  input  D_3,
  output O_0,
  output O_1,
  output O_2,
  output O_3
);

  wire register_simple_1_q_0, register_simple_1_q_1, register_simple_1_q_2, register_simple_1_q_3;

  register_simple register_simple_1 (
    .E_out(E_store), .CLK(CLK), .D_0(D_0), .D_1(D_1), .D_2(D_2), .D_3(D_3), .Q_0(register_simple_1_q_0),
    .Q_1(register_simple_1_q_1), .Q_2(register_simple_1_q_2), .Q_3(register_simple_1_q_3));
  tri_state_buffer_4bit tri_state_buffer_4bit_1 (
    .D_0(register_simple_1_q_0), .D_1(register_simple_1_q_1), .D_2(register_simple_1_q_2),
    .D_3(register_simple_1_q_3), .E(E_ouput), .O_0(O_0), .O_1(O_1), .O_2(O_2), .O_3(O_3));
endmodule
