// Digital circuit decoder-3-to-8.dig as structural Verilog
module decoder_3_to_8 (
  input  S_0,
  input  S_1,
  input  S_2,
  input  E,
  output O_0,
  output O_1,
  output O_2,
  output O_3,
  output O_4,
  output O_5,
  output O_6,
  output O_7
);

  wire and_1_out, and_2_out, not_1_out;

  not not_1 (not_1_out, S_2);
  and and_1 (and_1_out, not_1_out, E);
  and and_2 (and_2_out, S_2, E);
  decoder_2_to_4 decoder_2_to_4_1 (.S_0(S_0), .S_1(S_1), .E(and_1_out), .O_0(O_0), .O_1(O_1), .O_2(O_2), .O_3(O_3));
  decoder_2_to_4 decoder_2_to_4_2 (.S_0(S_0), .S_1(S_1), .E(and_2_out), .O_0(O_4), .O_1(O_5), .O_2(O_6), .O_3(O_7));
endmodule

/* Test case:
E  S_2 S_1 S_0  O_7 O_6 O_5 O_4 O_3 O_2 O_1 O_0 
0  x    x   x   bits(8, 0)
repeat(8) 1 bits(3, n) bits(8, 1<<n)
*/
