// Digital circuit experiments-counter.dig as structural Verilog
module experiments_counter (
  input  in_1,
  input  clk
);

  wire adder_1_p10, adder_1_p11, adder_1_p12, adder_1_p13, register_simple_1_q_0, register_simple_1_q_1,
       register_simple_1_q_2, register_simple_1_q_3;

  register_simple register_simple_1 (
    .E_out(in_1), .CLK(clk), .D_0(adder_1_p10), .D_1(adder_1_p11), .D_2(adder_1_p12), .D_3(adder_1_p13),
    .Q_0(register_simple_1_q_0), .Q_1(register_simple_1_q_1), .Q_2(register_simple_1_q_2),
    .Q_3(register_simple_1_q_3));
  // adder adder_1: pin names not known; wires that end beside it: 1'b1, 1'b0, 1'b0, 1'b0, 1'b0, register_simple_1_q_0, register_simple_1_q_1, register_simple_1_q_2, register_simple_1_q_3, adder_1_p10, adder_1_p11, adder_1_p12, adder_1_p13
  LED led_1 (.in(adder_1_p13));
  LED led_2 (.in(adder_1_p12));
  LED led_3 (.in(adder_1_p11));
  LED led_4 (.in(adder_1_p10));
endmodule
