// Digital circuit full-adder.dig as structural Verilog
module full_adder (
  input  c_in,
  input  i_1,
  input  i_2,
  output o,
  output c_out
);

  wire half_adder_1_c, half_adder_1_o, half_adder_2_c;

  half_adder half_adder_1 (.i_1(i_1), .i_2(i_2), .o(half_adder_1_o), .c(half_adder_1_c));
  half_adder half_adder_2 (.i_1(c_in), .i_2(half_adder_1_o), .o(o), .c(half_adder_2_c));
  or or_1 (c_out, half_adder_2_c, half_adder_1_c);

  // Notes on the sheet:
  //   c_in: 1 when we add 1 from previous operation
endmodule

/* Test case full-adder tests:
c_in i_1 i_2  o c_out

0 0 0    0 0
0 0 1    1 0
0 1 0    1 0
0 1 1    0 1
1 0 0    1 0
1 0 1    0 1
1 1 0    0 1
1 1 1    1 1
*/
