// Digital circuit half-adder.dig as structural Verilog
module half_adder (
  input  i_1,
  input  i_2,
  output o,
  output c
);

  xor xor_1 (o, i_1, i_2);
  and and_1 (c, i_1, i_2);

  // Notes on the sheet:
  //   o: sum
  //   c: carry out
endmodule

/* Test case half-adder tests:
           i_1 i_2   o c

repeat(4) bits(2, n) (n&1 ^ n>>1&1) x 
*/
