// Digital circuit memory.dig as structural Verilog
module memory (
  input  in_1,
  input  in_2,
  input  in_3,
  input  in_4,
  input  in_5,
  input  in_6,
  input  in_7,
  input  in_8,
  input  in_9,
  input  in_10,
  input  in_11,
  input  in_12,
  input  in_13,
  input  in_14,
  input  in_15,
  input  in_16,
  input  in_17
);

  wire and_1_out, and_2_out, and_3_out, nand_1_out, nand_2_out, nand_3_out, nand_4_out, nor_1_out, nor_2_out,
       nor_3_out, nor_flip_flop_1_q, nor_flip_flop_1_q_2, nor_flip_flop_2_q, nor_flip_flop_2_q_2, not_1_out,
       or_1_out, or_2_out, xnor_1_out, xor_1_out, xor_2_out, xor_3_out, xor_4_out;

  nand nand_1 (nand_1_out, in_1, xor_1_out);
  xor xor_1 (xor_1_out, nand_1_out, in_2);
  xnor xnor_1 (xnor_1_out, in_5, xnor_1_out);
  nor nor_1 (nor_1_out, in_12, nor_1_out);
  nand nand_2 (nand_2_out, in_6, nand_2_out);
  xor xor_2 (xor_2_out, in_4, xor_2_out);
  or or_1 (or_1_out, in_3, or_1_out);
  or or_2 (or_2_out, in_11, xor_3_out);
  xor xor_3 (xor_3_out, or_2_out, in_13);
  xor xor_4 (xor_4_out, in_7, and_1_out);
  and and_1 (and_1_out, xor_4_out, in_8);
  nand nand_3 (nand_3_out, in_9, nand_4_out);
  nand nand_4 (nand_4_out, nand_3_out, in_10);
  not not_1 (not_1_out, in_16);
  and and_2 (and_2_out, not_1_out, in_17);
  nor nor_2 (nor_2_out, in_14, nor_3_out);
  nor nor_3 (nor_3_out, nor_2_out, in_15);
  and and_3 (and_3_out, in_17, in_16);
  nor_flip_flop nor_flip_flop_1 (.S(and_3_out), .R(and_2_out), .Q(nor_flip_flop_1_q), .Q_2(nor_flip_flop_1_q_2));
  nor_flip_flop nor_flip_flop_2 (
    .S(nor_flip_flop_1_q_2), .R(nor_flip_flop_1_q), .Q(nor_flip_flop_2_q), .Q_2(nor_flip_flop_2_q_2));

  // Notes on the sheet:
  //   in_5: default 1
  //   in_12: default 1
  //   XNOR: oscilates when turned Off
  //   NOR: oscilates when turned off
  //   NAND: oscilates when turned on
  //   XOR: oscilates when turned on
  //   OR: only on, can't turn-off
endmodule
