// Digital circuit multiplexer-2.dig as structural Verilog
module multiplexer_2 (
  input  S,
  input  D_0,
  input  D_1,
  output O
);

  wire and_1_out, and_2_out, not_1_out;

  not not_1 (not_1_out, S);
  and and_1 (and_1_out, not_1_out, D_0);
  and and_2 (and_2_out, D_1, S);
  or or_1 (O, and_1_out, and_2_out);
endmodule

/* Test case:
S D_0 D_1 O

repeat(2) 0 bits(1,n) x bits(1,n)
repeat(2) 1 x bits(1,n) bits(1,n) 
*/
