// Digital circuit nor-flip-flop.dig as structural Verilog
module nor_flip_flop (
  input  S,
  input  R,
  output Q,
  output Q_2
);

  nor nor_1 (Q_2, S, Q);
  nor nor_2 (Q, Q_2, R);

  // Notes on the sheet:
  //   S: set
  //   R: reset
  //   possible also with NAND (with inversed truth table)
endmodule

/* Test case NOR SR flop-flop  tests:
S R Q -Q
0 0 x x
1 0 1 0
0 0 1 0
0 1 0 1
0 0 0 1
1 0 1 0

# 1 1 results in undefined state
*/
