// Digital circuit rising-edge-one-flip-flop.dig as structural Verilog
module rising_edge_one_flip_flop (
  input  in_1,
  input  in_2
);

  wire d_flip_flop_1_q, d_flip_flop_2_q, d_flip_flop_3_q, delay_1_out, not_1_out, xor_1_out;

  xor xor_1 (xor_1_out, in_1, delay_1_out);
  Delay #(.delayTime(10)) delay_1 (.in(in_1), .out(delay_1_out));
  D_flip_flop d_flip_flop_1 (.D(in_1), .CLK(xor_1_out), .Q(d_flip_flop_1_q));  // open: Q_2
  not not_1 (not_1_out, in_2);
  D_flip_flop d_flip_flop_2 (.D(in_2), .CLK(in_2), .Q(d_flip_flop_2_q));  // open: Q_2
  D_flip_flop d_flip_flop_3 (.D(d_flip_flop_2_q), .CLK(not_1_out), .Q(d_flip_flop_3_q));  // open: Q_2
endmodule
