// Digital circuit rom-buffer.dig as structural Verilog
module rom_buffer (
  input  E,
  input  [7:0] D,
  output O_0,
  output O_1,
  output O_2,
  output O_3,
  output O_4,
  output O_5,
  output O_6,
  output O_7
);

  tri_state_buffer_4bit tri_state_buffer_4bit_1 (
    .D_0(D[0]), .D_1(D[1]), .D_2(D[2]), .D_3(D[3]), .E(E), .O_0(O_0), .O_1(O_1), .O_2(O_2), .O_3(O_3));
  tri_state_buffer_4bit tri_state_buffer_4bit_2 (
    .D_0(D[4]), .D_1(D[5]), .D_2(D[6]), .D_3(D[7]), .E(E), .O_0(O_4), .O_1(O_5), .O_2(O_6), .O_3(O_7));
endmodule
