// Digital circuit rom.dig as structural Verilog
module rom (
  input  in_1,
  input  in_2,
  input  in_3,
  input  in_4,
  input  in_5,
  input  [5:0] in_6
);

  wire dipswitch_1_out, dipswitch_2_out, dipswitch_3_out, dipswitch_4_out, dipswitch_5_out, dipswitch_6_out;
  wire [5:0] dipswitch_7_out;

  DipSwitch dipswitch_1 (.out(dipswitch_1_out));
  DipSwitch dipswitch_2 (.out(dipswitch_2_out));
  DipSwitch dipswitch_3 (.out(dipswitch_3_out));
  DipSwitch dipswitch_4 (.out(dipswitch_4_out));
  DipSwitch dipswitch_5 (.out(dipswitch_5_out));
  DipSwitch dipswitch_6 (.out(dipswitch_6_out));
  DipSwitch dipswitch_7 (.out(dipswitch_7_out[5]));
  DipSwitch dipswitch_8 (.out(dipswitch_7_out[4]));
  DipSwitch dipswitch_9 (.out(dipswitch_7_out[3]));
  DipSwitch dipswitch_10 (.out(dipswitch_7_out[2]));
  DipSwitch dipswitch_11 (.out(dipswitch_7_out[1]));
  DipSwitch dipswitch_12 (.out(dipswitch_7_out[0]));

  // Notes on the sheet:
  //   in_6: default 4
endmodule
