// Digital circuit t-flip-flop.dig as structural Verilog
module t_flip_flop (
  input  C,
  output Q,
  output Q_2
);

  wire not_1_out;

  not not_1 (not_1_out, Q_2);
  rising_edge_d_flip_flop rising_edge_d_flip_flop_1 (.D(not_1_out), .CLK(C), .Q(Q_2), .Q_2(Q));
endmodule
