// Digital circuit test-rising-edge-detection.dig as structural Verilog
module test_rising_edge_detection (
  input  clk
);

  wire rising_edge_detector_1_o, t_flip_flop_1_q_2;

  rising_edge_detector rising_edge_detector_1 (.CLK(clk), .O(rising_edge_detector_1_o));
  t_flip_flop t_flip_flop_1 (.C(rising_edge_detector_1_o), .Q_2(t_flip_flop_1_q_2));  // open: Q
endmodule
