// Digital circuit tri-state-buffer-4bit.dig as structural Verilog
module tri_state_buffer_4bit (
  input  D_0,
  input  D_1,
  input  D_2,
  input  D_3,
  input  E,
  output O_0,
  output O_1,
  output O_2,
  output O_3
);

  assign O_0 = E ? D_0 : 1'bz;  // Driver driver_1
  assign O_1 = E ? D_1 : 1'bz;  // Driver driver_2
  assign O_2 = E ? D_2 : 1'bz;  // Driver driver_3
  assign O_3 = E ? D_3 : 1'bz;  // Driver driver_4

  // Notes on the sheet:
  //   E: enables output
endmodule

/* Test case:
E D_0 D_1 D_2 D_3 O_0 O_1 O_2 O_3

repeat(16) 0 bits(4, n) z z z z 
repeat(16) 1 bits(4, n) bits(4, n) 
*/
