// Digital circuit jk-flip-flop-rising-edge.dig as structural Verilog
module jk_flip_flop_rising_edge (
  input  S,
  input  R,
  input  C,
  output Q,
  output Q_2
);

  wire and_1_out, and_2_out, and_3_out, and_4_out, nor_1_out, nor_2_out, not_1_out;

  and and_1 (and_1_out, S, Q_2, C);
  and and_2 (and_2_out, C, Q, R);
  nor nor_1 (nor_1_out, and_1_out, nor_2_out);
  nor nor_2 (nor_2_out, nor_1_out, and_2_out);
  not not_1 (not_1_out, C);
  and and_3 (and_3_out, nor_2_out, not_1_out);
  and and_4 (and_4_out, not_1_out, nor_1_out);
  nor nor_3 (Q_2, and_3_out, Q);
  nor nor_4 (Q, Q_2, and_4_out);

  // Notes on the sheet:
  //   S: set
  //   R: reset
  //   rising edge toggling JK flip-flop without delay
endmodule
