// Digital circuit memory2.dig as structural Verilog
module memory2 (
  input  a_0,
  input  a_1,
  input  a_2,
  input  a_3,
  input  E,
  input  C,
  input  D_0,
  input  D_1,
  input  D_2,
  input  D_3,
  output O_0,
  output O_1,
  output O_2,
  output O_3
);

  wire and_1_out, and_2_out, and_3_out, and_4_out, and_5_out, and_6_out, and_7_out, and_8_out, and_9_out,
       and_10_out, and_11_out, and_12_out, and_13_out, and_14_out, and_15_out, and_16_out, and_17_out,
       and_18_out, and_19_out, and_20_out, and_21_out, and_22_out, and_23_out, and_24_out, and_25_out,
       and_26_out, and_27_out, and_28_out, and_29_out, and_30_out, and_31_out, and_32_out, not_1_out,
       not_2_out, not_3_out, not_4_out, register_simple_1_q_0, register_simple_1_q_1, register_simple_1_q_2,
       register_simple_1_q_3, register_simple_2_q_0, register_simple_2_q_1, register_simple_2_q_2,
       register_simple_2_q_3, register_simple_3_q_0, register_simple_3_q_1, register_simple_3_q_2,
       register_simple_3_q_3, register_simple_4_q_0, register_simple_4_q_1, register_simple_4_q_2,
       register_simple_4_q_3, register_simple_5_q_0, register_simple_5_q_1, register_simple_5_q_2,
       register_simple_5_q_3, register_simple_6_q_0, register_simple_6_q_1, register_simple_6_q_2,
       register_simple_6_q_3, register_simple_7_q_0, register_simple_7_q_1, register_simple_7_q_2,
       register_simple_7_q_3, register_simple_8_q_0, register_simple_8_q_1, register_simple_8_q_2,
       register_simple_8_q_3, register_simple_9_q_0, register_simple_9_q_1, register_simple_9_q_2,
       register_simple_9_q_3, register_simple_10_q_0, register_simple_10_q_1, register_simple_10_q_2,
       register_simple_10_q_3, register_simple_11_q_0, register_simple_11_q_1, register_simple_11_q_2,
       register_simple_11_q_3, register_simple_12_q_0, register_simple_12_q_1, register_simple_12_q_2,
       register_simple_12_q_3, register_simple_13_q_0, register_simple_13_q_1, register_simple_13_q_2,
       register_simple_13_q_3, register_simple_14_q_0, register_simple_14_q_1, register_simple_14_q_2,
       register_simple_14_q_3, register_simple_15_q_0, register_simple_15_q_1, register_simple_15_q_2,
       register_simple_15_q_3, register_simple_16_q_0, register_simple_16_q_1, register_simple_16_q_2,
       register_simple_16_q_3;

  not not_1 (not_1_out, a_3);
  not not_2 (not_2_out, a_2);
  not not_3 (not_3_out, a_1);
  not not_4 (not_4_out, a_0);
  and and_1 (and_1_out, not_4_out, not_3_out, not_2_out, not_1_out);
  and and_2 (and_2_out, a_0, not_3_out, not_2_out, not_1_out);
  and and_3 (and_3_out, not_4_out, a_1, not_2_out, not_1_out);
  and and_4 (and_4_out, a_0, a_1, not_2_out, not_1_out);
  and and_5 (and_5_out, not_4_out, not_3_out, a_2, not_1_out);
  and and_6 (and_6_out, a_0, not_3_out, a_2, not_1_out);
  and and_7 (and_7_out, not_4_out, a_1, a_2, not_1_out);
  and and_8 (and_8_out, a_0, a_1, a_2, not_1_out);
  and and_9 (and_9_out, not_4_out, not_3_out, not_2_out, a_3);
  and and_10 (and_10_out, a_0, not_3_out, not_2_out, a_3);
  and and_11 (and_11_out, not_4_out, a_1, not_2_out, a_3);
  and and_12 (and_12_out, a_0, a_1, not_2_out, a_3);
  and and_13 (and_13_out, not_4_out, not_3_out, a_2, a_3);
  and and_14 (and_14_out, a_0, not_3_out, a_2, a_3);
  and and_15 (and_15_out, not_4_out, a_1, a_2, a_3);
  and and_16 (and_16_out, a_0, a_1, a_2, a_3);
  and and_17 (and_17_out, E, and_1_out);
  and and_18 (and_18_out, E, and_2_out);
  and and_19 (and_19_out, E, and_3_out);
  and and_20 (and_20_out, E, and_4_out);
  and and_21 (and_21_out, E, and_5_out);
  and and_22 (and_22_out, E, and_6_out);
  and and_23 (and_23_out, E, and_7_out);
  and and_24 (and_24_out, E, and_8_out);
  and and_25 (and_25_out, E, and_9_out);
  and and_26 (and_26_out, E, and_10_out);
  and and_27 (and_27_out, E, and_11_out);
  and and_28 (and_28_out, E, and_12_out);
  and and_29 (and_29_out, E, and_13_out);
  and and_30 (and_30_out, E, and_14_out);
  and and_31 (and_31_out, E, and_15_out);
  and and_32 (and_32_out, E, and_16_out);
  register_simple register_simple_1 (
    .E_out(and_17_out), .CLK(C), .D_0(D_0), .D_1(D_1), .D_2(D_2), .D_3(D_3), .Q_0(register_simple_1_q_0),
    .Q_1(register_simple_1_q_1), .Q_2(register_simple_1_q_2), .Q_3(register_simple_1_q_3));
  register_simple register_simple_2 (
    .E_out(and_18_out), .CLK(C), .D_0(D_0), .D_1(D_1), .D_2(D_2), .D_3(D_3), .Q_0(register_simple_2_q_0),
    .Q_1(register_simple_2_q_1), .Q_2(register_simple_2_q_2), .Q_3(register_simple_2_q_3));
  register_simple register_simple_3 (
    .E_out(and_19_out), .CLK(C), .D_0(D_0), .D_1(D_1), .D_2(D_2), .D_3(D_3), .Q_0(register_simple_3_q_0),
    .Q_1(register_simple_3_q_1), .Q_2(register_simple_3_q_2), .Q_3(register_simple_3_q_3));
  register_simple register_simple_4 (
    .E_out(and_20_out), .CLK(C), .D_0(D_0), .D_1(D_1), .D_2(D_2), .D_3(D_3), .Q_0(register_simple_4_q_0),
    .Q_1(register_simple_4_q_1), .Q_2(register_simple_4_q_2), .Q_3(register_simple_4_q_3));
  register_simple register_simple_5 (
    .E_out(and_21_out), .CLK(C), .D_0(D_0), .D_1(D_1), .D_2(D_2), .D_3(D_3), .Q_0(register_simple_5_q_0),
    .Q_1(register_simple_5_q_1), .Q_2(register_simple_5_q_2), .Q_3(register_simple_5_q_3));
  register_simple register_simple_6 (
    .E_out(and_22_out), .CLK(C), .D_0(D_0), .D_1(D_1), .D_2(D_2), .D_3(D_3), .Q_0(register_simple_6_q_0),
    .Q_1(register_simple_6_q_1), .Q_2(register_simple_6_q_2), .Q_3(register_simple_6_q_3));
  register_simple register_simple_7 (
    .E_out(and_23_out), .CLK(C), .D_0(D_0), .D_1(D_1), .D_2(D_2), .D_3(D_3), .Q_0(register_simple_7_q_0),
    .Q_1(register_simple_7_q_1), .Q_2(register_simple_7_q_2), .Q_3(register_simple_7_q_3));
  register_simple register_simple_8 (
    .E_out(and_24_out), .CLK(C), .D_0(D_0), .D_1(D_1), .D_2(D_2), .D_3(D_3), .Q_0(register_simple_8_q_0),
    .Q_1(register_simple_8_q_1), .Q_2(register_simple_8_q_2), .Q_3(register_simple_8_q_3));
  register_simple register_simple_9 (
    .E_out(and_25_out), .CLK(C), .D_0(D_0), .D_1(D_1), .D_2(D_2), .D_3(D_3), .Q_0(register_simple_9_q_0),
    .Q_1(register_simple_9_q_1), .Q_2(register_simple_9_q_2), .Q_3(register_simple_9_q_3));
  register_simple register_simple_10 (
    .E_out(and_26_out), .CLK(C), .D_0(D_0), .D_1(D_1), .D_2(D_2), .D_3(D_3), .Q_0(register_simple_10_q_0),
    .Q_1(register_simple_10_q_1), .Q_2(register_simple_10_q_2), .Q_3(register_simple_10_q_3));
  register_simple register_simple_11 (
    .E_out(and_27_out), .CLK(C), .D_0(D_0), .D_1(D_1), .D_2(D_2), .D_3(D_3), .Q_0(register_simple_11_q_0),
    .Q_1(register_simple_11_q_1), .Q_2(register_simple_11_q_2), .Q_3(register_simple_11_q_3));
  register_simple register_simple_12 (
    .E_out(and_28_out), .CLK(C), .D_0(D_0), .D_1(D_1), .D_2(D_2), .D_3(D_3), .Q_0(register_simple_12_q_0),
    .Q_1(register_simple_12_q_1), .Q_2(register_simple_12_q_2), .Q_3(register_simple_12_q_3));
  register_simple register_simple_13 (
    .E_out(and_29_out), .CLK(C), .D_0(D_0), .D_1(D_1), .D_2(D_2), .D_3(D_3), .Q_0(register_simple_13_q_0),
    .Q_1(register_simple_13_q_1), .Q_2(register_simple_13_q_2), .Q_3(register_simple_13_q_3));
  register_simple register_simple_14 (
    .E_out(and_30_out), .CLK(C), .D_0(D_0), .D_1(D_1), .D_2(D_2), .D_3(D_3), .Q_0(register_simple_14_q_0),
    .Q_1(register_simple_14_q_1), .Q_2(register_simple_14_q_2), .Q_3(register_simple_14_q_3));
  register_simple register_simple_15 (
    .E_out(and_31_out), .CLK(C), .D_0(D_0), .D_1(D_1), .D_2(D_2), .D_3(D_3), .Q_0(register_simple_15_q_0),
    .Q_1(register_simple_15_q_1), .Q_2(register_simple_15_q_2), .Q_3(register_simple_15_q_3));
  register_simple register_simple_16 (
    .E_out(and_32_out), .CLK(C), .D_0(D_0), .D_1(D_1), .D_2(D_2), .D_3(D_3), .Q_0(register_simple_16_q_0),
    .Q_1(register_simple_16_q_1), .Q_2(register_simple_16_q_2), .Q_3(register_simple_16_q_3));
  assign O_0 = and_1_out ? register_simple_1_q_0 : 1'bz;  // Driver driver_1
  assign O_1 = and_1_out ? register_simple_1_q_1 : 1'bz;  // Driver driver_2
  assign O_0 = and_2_out ? register_simple_2_q_0 : 1'bz;  // Driver driver_3
  assign O_1 = and_2_out ? register_simple_2_q_1 : 1'bz;  // Driver driver_4
  assign O_0 = and_3_out ? register_simple_3_q_0 : 1'bz;  // Driver driver_5
  assign O_1 = and_3_out ? register_simple_3_q_1 : 1'bz;  // Driver driver_6
  assign O_0 = and_4_out ? register_simple_4_q_0 : 1'bz;  // Driver driver_7
  assign O_1 = and_4_out ? register_simple_4_q_1 : 1'bz;  // Driver driver_8
  assign O_0 = and_5_out ? register_simple_5_q_0 : 1'bz;  // Driver driver_9
  assign O_1 = and_5_out ? register_simple_5_q_1 : 1'bz;  // Driver driver_10
  assign O_0 = and_6_out ? register_simple_6_q_0 : 1'bz;  // Driver driver_11
  assign O_1 = and_6_out ? register_simple_6_q_1 : 1'bz;  // Driver driver_12
  assign O_0 = and_7_out ? register_simple_7_q_0 : 1'bz;  // Driver driver_13
  assign O_1 = and_7_out ? register_simple_7_q_1 : 1'bz;  // Driver driver_14
  assign O_0 = and_8_out ? register_simple_8_q_0 : 1'bz;  // Driver driver_15
  assign O_1 = and_8_out ? register_simple_8_q_1 : 1'bz;  // Driver driver_16
  assign O_0 = and_9_out ? register_simple_9_q_0 : 1'bz;  // Driver driver_17
  assign O_1 = and_9_out ? register_simple_9_q_1 : 1'bz;  // Driver driver_18
  assign O_0 = and_10_out ? register_simple_10_q_0 : 1'bz;  // Driver driver_19
  assign O_1 = and_10_out ? register_simple_10_q_1 : 1'bz;  // Driver driver_20
  assign O_0 = and_11_out ? register_simple_11_q_0 : 1'bz;  // Driver driver_21
  assign O_1 = and_11_out ? register_simple_11_q_1 : 1'bz;  // Driver driver_22
  assign O_0 = and_12_out ? register_simple_12_q_0 : 1'bz;  // Driver driver_23
  assign O_1 = and_12_out ? register_simple_12_q_1 : 1'bz;  // Driver driver_24
  assign O_0 = and_13_out ? register_simple_13_q_0 : 1'bz;  // Driver driver_25
  assign O_1 = and_13_out ? register_simple_13_q_1 : 1'bz;  // Driver driver_26
  assign O_0 = and_14_out ? register_simple_14_q_0 : 1'bz;  // Driver driver_27
  assign O_1 = and_14_out ? register_simple_14_q_1 : 1'bz;  // Driver driver_28
  assign O_0 = and_15_out ? register_simple_15_q_0 : 1'bz;  // Driver driver_29
  assign O_1 = and_15_out ? register_simple_15_q_1 : 1'bz;  // Driver driver_30
  assign O_0 = and_16_out ? register_simple_16_q_0 : 1'bz;  // Driver driver_31
  assign O_1 = and_16_out ? register_simple_16_q_1 : 1'bz;  // Driver driver_32
  assign O_2 = and_1_out ? register_simple_1_q_2 : 1'bz;  // Driver driver_33
  assign O_2 = and_2_out ? register_simple_2_q_2 : 1'bz;  // Driver driver_34
  assign O_2 = and_3_out ? register_simple_3_q_2 : 1'bz;  // Driver driver_35
  assign O_2 = and_4_out ? register_simple_4_q_2 : 1'bz;  // Driver driver_36
  assign O_2 = and_5_out ? register_simple_5_q_2 : 1'bz;  // Driver driver_37
  assign O_2 = and_6_out ? register_simple_6_q_2 : 1'bz;  // Driver driver_38
  assign O_2 = and_7_out ? register_simple_7_q_2 : 1'bz;  // Driver driver_39
  assign O_2 = and_8_out ? register_simple_8_q_2 : 1'bz;  // Driver driver_40
  assign O_2 = and_9_out ? register_simple_9_q_2 : 1'bz;  // Driver driver_41
  assign O_2 = and_10_out ? register_simple_10_q_2 : 1'bz;  // Driver driver_42
  assign O_2 = and_11_out ? register_simple_11_q_2 : 1'bz;  // Driver driver_43
  assign O_2 = and_12_out ? register_simple_12_q_2 : 1'bz;  // Driver driver_44
  assign O_2 = and_13_out ? register_simple_13_q_2 : 1'bz;  // Driver driver_45
  assign O_2 = and_14_out ? register_simple_14_q_2 : 1'bz;  // Driver driver_46
  assign O_2 = and_15_out ? register_simple_15_q_2 : 1'bz;  // Driver driver_47
  assign O_2 = and_16_out ? register_simple_16_q_2 : 1'bz;  // Driver driver_48
  assign O_3 = and_1_out ? register_simple_1_q_3 : 1'bz;  // Driver driver_49
  assign O_3 = and_2_out ? register_simple_2_q_3 : 1'bz;  // Driver driver_50
  assign O_3 = and_3_out ? register_simple_3_q_3 : 1'bz;  // Driver driver_51
  assign O_3 = and_4_out ? register_simple_4_q_3 : 1'bz;  // Driver driver_52
  assign O_3 = and_5_out ? register_simple_5_q_3 : 1'bz;  // Driver driver_53
  assign O_3 = and_6_out ? register_simple_6_q_3 : 1'bz;  // Driver driver_54
  assign O_3 = and_7_out ? register_simple_7_q_3 : 1'bz;  // Driver driver_55
  assign O_3 = and_8_out ? register_simple_8_q_3 : 1'bz;  // Driver driver_56
  assign O_3 = and_9_out ? register_simple_9_q_3 : 1'bz;  // Driver driver_57
  assign O_3 = and_10_out ? register_simple_10_q_3 : 1'bz;  // Driver driver_58
  assign O_3 = and_11_out ? register_simple_11_q_3 : 1'bz;  // Driver driver_59
  assign O_3 = and_12_out ? register_simple_12_q_3 : 1'bz;  // Driver driver_60
  assign O_3 = and_13_out ? register_simple_13_q_3 : 1'bz;  // Driver driver_61
  assign O_3 = and_14_out ? register_simple_14_q_3 : 1'bz;  // Driver driver_62
  assign O_3 = and_15_out ? register_simple_15_q_3 : 1'bz;  // Driver driver_63
  assign O_3 = and_16_out ? register_simple_16_q_3 : 1'bz;  // Driver driver_64

  // Notes on the sheet:
  //   0
  //   4
  //   8
  //   12
  //   15
endmodule

/* Test case:
C E   a_0 a_1 a_2 a_3   D_0 D_1 D_2 D_3   O_0 O_1 O_2 O_3

loop(v, 16)
 # save
 repeat(16)     C 1 bits(4, n)    bits(4, v)        bits(4, v)
 # read ignoring data
 repeat(16)     0 0 bits(4, n)    x x x x        bits(4, v)
 repeat(16)     0 1 bits(4, n)    bits(4, ~v)    bits(4, v)
 repeat(16)     C 0 bits(4, n)    bits(4, ~v)    bits(4, v)
end loop
*/
