// Digital circuit notepad.dig as structural Verilog
module notepad (
  input  D,
  input  CLK,
  input  C,
  input  R_a,
  input  S,
  input  D_0,
  input  D_1,
  output Q,
  output Q_2,
  output O_0,
  output O_1
);

  wire and_1_out, d_flip_flop_1_q, multiplexer_2_1_o, multiplexer_2_2_o, multiplexer_2_3_o,
       multiplexer_2_4_o, multiplexer_2_5_o, not_1_out, not_2_out, not_3_out, not_4_out, not_5_out, or_1_out,
       rising_edge_d_flip_flop_1_q, rising_edge_detector_1_o, undriven, undriven_2, undriven_3, undriven_4,
       undriven_5, undriven_6;

  not not_1 (not_1_out, rising_edge_d_flip_flop_1_q);
  or or_1 (or_1_out, undriven_4, undriven_5);
  multiplexer_2 multiplexer_2_1 (.D_0(not_1_out), .D_1(undriven_6), .O(multiplexer_2_1_o));  // open: S
  not not_2 (not_2_out, D_0);
  not not_3 (not_3_out, D_1);
  and and_1 (and_1_out, undriven_3, or_1_out);
  multiplexer_2 multiplexer_2_2 (.S(S), .D_0(1'b1), .D_1(D_0), .O(multiplexer_2_2_o));
  multiplexer_2 multiplexer_2_3 (.S(S), .D_0(1'b1), .D_1(not_2_out), .O(multiplexer_2_3_o));
  multiplexer_2 multiplexer_2_4 (.S(S), .D_0(1'b1), .D_1(D_1), .O(multiplexer_2_4_o));
  multiplexer_2 multiplexer_2_5 (.S(S), .D_0(1'b1), .D_1(not_3_out), .O(multiplexer_2_5_o));
  rising_edge_detector rising_edge_detector_1 (.CLK(C), .O(rising_edge_detector_1_o));
  rising_edge_d_flip_flop rising_edge_d_flip_flop_1 (
    .D(undriven_2), .Q(rising_edge_d_flip_flop_1_q));  // open: CLK, Q_2
  // Or or_2 has open pins: In_1=undriven, In_2=and_1_out, out=open
  not not_4 (not_4_out, CLK);
  JK_async_resetable_flip_flop jk_async_resetable_flip_flop_1 (
    .C(rising_edge_detector_1_o), .S(multiplexer_2_2_o), .R(multiplexer_2_3_o), .R_a(R_a), .Q(O_0));  // open: Q_2
  JK_async_resetable_flip_flop jk_async_resetable_flip_flop_2 (
    .C(O_0), .S(multiplexer_2_4_o), .R(multiplexer_2_5_o), .R_a(R_a), .Q(O_1));  // open: Q_2
  D_flip_flop d_flip_flop_1 (.D(D), .CLK(not_4_out), .Q(d_flip_flop_1_q));  // open: Q_2
  not not_5 (not_5_out, not_4_out);
  D_flip_flop d_flip_flop_2 (.D(d_flip_flop_1_q), .CLK(not_5_out), .Q(Q), .Q_2(Q_2));

  // Notes on the sheet:
  //   R_a: reset async
  //   reset
  //   D
  //   set
  //   set/reset counter
  //   clock
  //   previous flip-flop
  //   generate test headers
  //   tryhaskell.org
  //   concat $ map (\x -> " D_" ++ show x) [63,62..0]
  //   rising edge D flip-flop without delay
  //   clock input signal
endmodule
