// Digital circuit register-simple.dig as structural Verilog
module register_simple (
  input  E_out,
  input  CLK,
  input  D_0,
  input  D_1,
  input  D_2,
  input  D_3,
  output Q_0,
  output Q_1,
  output Q_2,
  output Q_3
);

  wire and_1_out;

  and and_1 (and_1_out, CLK, E_out);
  rising_edge_d_flip_flop rising_edge_d_flip_flop_1 (.D(D_3), .CLK(and_1_out), .Q(Q_3));  // open: Q_2
  rising_edge_d_flip_flop rising_edge_d_flip_flop_2 (.D(D_2), .CLK(and_1_out), .Q(Q_2));  // open: Q_2
  rising_edge_d_flip_flop rising_edge_d_flip_flop_3 (.D(D_1), .CLK(and_1_out), .Q(Q_1));  // open: Q_2
  rising_edge_d_flip_flop rising_edge_d_flip_flop_4 (.D(D_0), .CLK(and_1_out), .Q(Q_0));  // open: Q_2

  // Notes on the sheet:
  //   E_out: enable write to the register
endmodule
