// Digital circuit register.dig as structural Verilog
module register (
  input  D_0,
  input  E_out,
  input  clk,
  input  D_1,
  input  D_2,
  input  D_3
);

  wire d_flip_flop_1_q, d_flip_flop_2_q, d_flip_flop_3_q, d_flip_flop_4_q, driver_1_out, driver_2_out,
       driver_3_out, driver_4_out, not_1_out;

  not not_1 (not_1_out, E_out);
  assign driver_1_out = not_1_out ? D_3 : 1'bz;  // Driver driver_1
  assign driver_2_out = not_1_out ? D_2 : 1'bz;  // Driver driver_2
  assign driver_3_out = not_1_out ? D_1 : 1'bz;  // Driver driver_3
  assign driver_4_out = not_1_out ? D_0 : 1'bz;  // Driver driver_4
  D_flip_flop d_flip_flop_1 (.D(driver_1_out), .CLK(clk), .Q(d_flip_flop_1_q));  // open: Q_2
  D_flip_flop d_flip_flop_2 (.D(driver_2_out), .CLK(clk), .Q(d_flip_flop_2_q));  // open: Q_2
  D_flip_flop d_flip_flop_3 (.D(driver_3_out), .CLK(clk), .Q(d_flip_flop_3_q));  // open: Q_2
  D_flip_flop d_flip_flop_4 (.D(driver_4_out), .CLK(clk), .Q(d_flip_flop_4_q));  // open: Q_2
  assign D_3 = E_out ? d_flip_flop_1_q : 1'bz;  // Driver driver_5
  assign D_2 = E_out ? d_flip_flop_2_q : 1'bz;  // Driver driver_6
  assign D_1 = E_out ? d_flip_flop_3_q : 1'bz;  // Driver driver_7
  assign D_0 = E_out ? d_flip_flop_4_q : 1'bz;  // Driver driver_8

  // Notes on the sheet:
  //   E_out: enable output. output to D
endmodule
