// Digital circuit reset-detector.dig as structural Verilog
module reset_detector (
  input  clk
);

  wire not_1_out, or_1_out, or_2_out, xor_1_out;

  not not_1 (not_1_out, clk);
  or or_1 (or_1_out, not_1_out, or_1_out);
  or or_2 (or_2_out, clk, or_2_out);
  xor xor_1 (xor_1_out, or_1_out, or_2_out);
endmodule
