// Digital circuit rising-edge-d-flip-flop.dig as structural Verilog
// stores value on a rising edge and shows new value on the output when rising edge is finished
module rising_edge_d_flip_flop (
  input  D,
  input  CLK,
  output Q,
  output Q_2
);

  wire and_1_out, d_flip_flop_1_q, delay_1_out, not_1_out, not_2_out;

  Delay #(.delayTime(2)) delay_1 (.in(CLK), .out(delay_1_out));
  not not_1 (not_1_out, delay_1_out);
  and and_1 (and_1_out, CLK, not_1_out);
  D_flip_flop d_flip_flop_1 (.D(D), .CLK(and_1_out), .Q(d_flip_flop_1_q));  // open: Q_2
  not not_2 (not_2_out, and_1_out);
  D_flip_flop d_flip_flop_2 (.D(d_flip_flop_1_q), .CLK(not_2_out), .Q(Q), .Q_2(Q_2));
endmodule

/* Test case:
CLK D Q -Q
  0 0 x x
  1 0 0 1
  1 1 0 1
  0 0 0 1
  0 1 0 1
  1 1 1 0
  1 0 1 0
  0 0 1 0
*/
