// Digital circuit rising-edge-detector.dig as structural Verilog
// sends a short pulse on a rising edge
module rising_edge_detector (
  input  CLK,
  output O
);

  wire delay_1_out, not_1_out;

  Delay #(.delayTime(2), .generic("this.Duration = args.duration;")) delay_1 (.in(CLK), .out(delay_1_out));
  not not_1 (not_1_out, delay_1_out);
  and and_1 (O, CLK, not_1_out);
endmodule
