// Digital circuit test-resetable-counter.dig as structural Verilog
module test_resetable_counter (
  input  S,
  input  D_0,
  input  R,
  input  C,
  input  D_1,
  input  D_2,
  input  D_3,
  output O_0,
  output O_1,
  output O_2,
  output O_3
);

  wire adder_1_p10, adder_1_p11, adder_1_p12, adder_1_p13, multiplexer_2_1_o, multiplexer_2_2_o,
       multiplexer_2_3_o, multiplexer_2_4_o, multiplexer_2_5_o, multiplexer_2_6_o, multiplexer_2_7_o,
       multiplexer_2_8_o;

  // adder adder_1: pin names not known; wires that end beside it: 1'b1, O_0, O_1, O_2, O_3, 1'b0, 1'b0, 1'b0, 1'b0, adder_1_p10, adder_1_p11, adder_1_p12, adder_1_p13
  multiplexer_2 multiplexer_2_1 (.S(S), .D_0(adder_1_p10), .D_1(D_0), .O(multiplexer_2_1_o));
  multiplexer_2 multiplexer_2_2 (.S(S), .D_0(adder_1_p11), .D_1(D_1), .O(multiplexer_2_2_o));
  multiplexer_2 multiplexer_2_3 (.S(S), .D_0(adder_1_p12), .D_1(D_2), .O(multiplexer_2_3_o));
  multiplexer_2 multiplexer_2_4 (.S(S), .D_0(adder_1_p13), .D_1(D_3), .O(multiplexer_2_4_o));
  multiplexer_2 multiplexer_2_5 (.S(R), .D_0(multiplexer_2_1_o), .D_1(1'b0), .O(multiplexer_2_5_o));
  multiplexer_2 multiplexer_2_6 (.S(R), .D_0(multiplexer_2_2_o), .D_1(1'b0), .O(multiplexer_2_6_o));
  multiplexer_2 multiplexer_2_7 (.S(R), .D_0(multiplexer_2_3_o), .D_1(1'b0), .O(multiplexer_2_7_o));
  multiplexer_2 multiplexer_2_8 (.S(R), .D_0(multiplexer_2_4_o), .D_1(1'b0), .O(multiplexer_2_8_o));
  register_simple register_simple_1 (
    .E_out(1'b1), .CLK(C), .D_0(multiplexer_2_5_o), .D_1(multiplexer_2_6_o), .D_2(multiplexer_2_7_o),
    .D_3(multiplexer_2_8_o), .Q_0(O_0), .Q_1(O_1), .Q_2(O_2), .Q_3(O_3));
endmodule
