// Digital circuit wip-counter-resetable.dig as structural Verilog
module wip_counter_resetable (
  input  C,
  input  R_a,
  input  S,
  input  D_0,
  input  D_1,
  input  D_2,
  input  D_3,
  output O_0,
  output O_1,
  output O_2,
  output O_3
);

  wire multiplexer_2_1_o, multiplexer_2_2_o, multiplexer_2_3_o, multiplexer_2_4_o, multiplexer_2_5_o,
       multiplexer_2_6_o, multiplexer_2_7_o, multiplexer_2_8_o, not_1_out, not_2_out, not_3_out, not_4_out,
       rising_edge_detector_1_o;

  not not_1 (not_1_out, D_0);
  not not_2 (not_2_out, D_1);
  not not_3 (not_3_out, D_2);
  not not_4 (not_4_out, D_3);
  rising_edge_detector rising_edge_detector_1 (.CLK(C), .O(rising_edge_detector_1_o));
  multiplexer_2 multiplexer_2_1 (.S(S), .D_0(1'b1), .D_1(D_0), .O(multiplexer_2_1_o));
  multiplexer_2 multiplexer_2_2 (.S(S), .D_0(1'b1), .D_1(not_1_out), .O(multiplexer_2_2_o));
  multiplexer_2 multiplexer_2_3 (.S(S), .D_0(1'b1), .D_1(D_1), .O(multiplexer_2_3_o));
  multiplexer_2 multiplexer_2_4 (.S(S), .D_0(1'b1), .D_1(not_2_out), .O(multiplexer_2_4_o));
  multiplexer_2 multiplexer_2_5 (.S(S), .D_0(1'b1), .D_1(D_2), .O(multiplexer_2_5_o));
  multiplexer_2 multiplexer_2_6 (.S(S), .D_0(1'b1), .D_1(not_3_out), .O(multiplexer_2_6_o));
  multiplexer_2 multiplexer_2_7 (.S(S), .D_0(1'b1), .D_1(D_3), .O(multiplexer_2_7_o));
  multiplexer_2 multiplexer_2_8 (.S(S), .D_0(1'b1), .D_1(not_4_out), .O(multiplexer_2_8_o));
  JK_async_resetable_flip_flop jk_async_resetable_flip_flop_1 (
    .C(rising_edge_detector_1_o), .S(multiplexer_2_1_o), .R(multiplexer_2_2_o), .R_a(R_a), .Q(O_0));  // open: Q_2
  JK_async_resetable_flip_flop jk_async_resetable_flip_flop_2 (
    .C(O_0), .S(multiplexer_2_3_o), .R(multiplexer_2_4_o), .R_a(R_a), .Q(O_1));  // open: Q_2
  JK_async_resetable_flip_flop jk_async_resetable_flip_flop_3 (
    .C(O_1), .S(multiplexer_2_5_o), .R(multiplexer_2_6_o), .R_a(R_a), .Q(O_2));  // open: Q_2
  JK_async_resetable_flip_flop jk_async_resetable_flip_flop_4 (
    .C(O_2), .S(multiplexer_2_7_o), .R(multiplexer_2_8_o), .R_a(R_a), .Q(O_3));  // open: Q_2

  // Notes on the sheet:
  //   R_a: reset async
  //   multiplexer can be simplified if D_0 is always 1
  //   setting is broken
endmodule
