// Digital circuit xor-test.dig as structural Verilog
module xor_test (
  input  i1,
  input  i2,
  output o1
);

  xor xor_1 (o1, i1, i2);
endmodule

/* Test case xor-tests:
           i1 i2       o1
#1  0   1
repeat(4) bits(2, n) ((n&1) ^ ((n &2)>>1))
*/
